// Logisim project test.alu.flag.circ as structural Verilog: 1 circuit, main circuit main
module main (
);

  wire alu_c, alu_m, alu_o_ab, alu_o_c, alu_o_g, alu_o_o, alu_o_p, alu_o_z, alu_sh, n7408_1_pin2,
       n7408_1_pin3, n7408_1_pin5, n7408_1_pin6, n7408_1_pin8, n7408_1_pin9, n7408_1_pin11, n7432_1_pin5,
       n7432_1_pin6, n7432_1_pin11;
  wire [3:0] A, alu_o_s, alu_out, alu_s, B, shift_o;

  _74157 #(.ShowInternalStructure("true")) u_74157_1 (
    .pin1(alu_sh), .pin2(alu_o_s[0]), .pin3(shift_o[0]), .pin4(alu_out[0]), .pin5(alu_o_s[1]),
    .pin6(shift_o[1]), .pin7(alu_out[1]), .pin14(alu_o_s[3]), .pin13(shift_o[3]), .pin12(alu_out[3]),
    .pin11(alu_o_s[2]), .pin10(shift_o[2]), .pin9(alu_out[2]));  // open: pin15
  DipSwitch #(.number(4)) dipswitch_1 (.sw1(A[0]), .sw2(A[1]), .sw3(A[2]), .sw4(A[3]));
  DipSwitch #(.number(7)) dipswitch_2 (
    .sw1(alu_s[0]), .sw2(alu_s[1]), .sw3(alu_s[2]), .sw4(alu_s[3]), .sw5(alu_c), .sw6(alu_m), .sw7(alu_sh));
  DipSwitch #(.number(4)) dipswitch_3 (.sw1(B[0]), .sw2(B[1]), .sw3(B[2]), .sw4(B[3]));
  // _74181 #(.ShowInternalStructure("true")) 74181_1: pin names not known; wires that end beside it: B[0], B[1], A[0], A[1], alu_s[3], B[2], alu_s[2], A[2], alu_s[1], B[3], alu_s[0], A[3], alu_c, alu_o_g, alu_m, alu_o_c, alu_o_s[0], alu_o_p, alu_o_s[1], alu_o_ab, alu_o_s[2], alu_o_s[3]
  _7408 #(.ShowInternalStructure("true")) u_7408_1 (
    .pin2(n7408_1_pin2), .pin3(n7408_1_pin3), .pin4(n7408_1_pin3), .pin5(n7408_1_pin5), .pin6(n7408_1_pin6),
    .pin13(B[3]), .pin12(A[3]), .pin11(n7408_1_pin11), .pin10(n7408_1_pin11), .pin9(n7408_1_pin9),
    .pin8(n7408_1_pin8));  // open: pin1
  _7432 #(.ShowInternalStructure("true")) u_7432_1 (
    .pin1(n7408_1_pin8), .pin2(n7408_1_pin6), .pin3(alu_o_o), .pin4(alu_out[3]), .pin5(n7432_1_pin5),
    .pin6(n7432_1_pin6), .pin13(alu_out[0]), .pin12(alu_out[1]), .pin11(n7432_1_pin11),
    .pin10(n7432_1_pin11), .pin9(alu_out[2]), .pin8(n7432_1_pin5));
  _7404 #(.ShowInternalStructure("true")) u_7404_1 (
    .pin1(B[3]), .pin2(n7408_1_pin2), .pin3(A[3]), .pin4(n7408_1_pin5), .pin11(alu_out[3]),
    .pin10(n7408_1_pin9), .pin9(n7432_1_pin6), .pin8(alu_o_z));  // open: pin5, pin6, pin13, pin12
  _74157 #(.ShowInternalStructure("true")) u_74157_2 (
    .pin1(alu_m), .pin2(A[1]), .pin4(shift_o[0]), .pin5(A[2]), .pin6(A[0]), .pin7(shift_o[1]), .pin13(A[2]),
    .pin12(shift_o[3]), .pin11(A[3]), .pin10(A[1]), .pin9(shift_o[2]));  // open: pin3, pin15, pin14
endmodule
